# Fritzing sketch Schematic (saved by Fritzing 0.9.3b)
breadboards: 1

parts:
  Composant1 = Adafruit ADS1115 16Bit I2C ADC [part_number="Adafruit #1085"]
  Raspberry_Pi_1 = Raspberry Pi 4 [part_number=RPI-4-b]
  R1 = Resistor [tolerance=±5% resistance=150 package=THT]
  R2 = Resistor [tolerance=±5% resistance=150 package=THT]
  R3 = Resistor [tolerance=±5% resistance=150 package=THT]
  R4 = Resistor [tolerance=±5% resistance=150 package=THT]
  D1 = Zener Diode [part_number=1N4732A breakdown_voltage=3.3V package="300 mil [THT]"]
  D2 = Zener Diode [part_number=1N4732A breakdown_voltage=3.3V package="300 mil [THT]"]
  R5 = Resistor [tolerance=±5% resistance=220 package=THT]
  R6 = Resistor [tolerance=±5% resistance=220 package=THT]
  Q2 = Basic FET N-Channel [package="D2Pak [SMD]"]
  Q3 = Basic FET N-Channel [package="D2Pak [SMD]"]
  Q4 = Basic FET N-Channel [package="D2Pak [SMD]"]
  R7 = Resistor [tolerance=±5% resistance=220 package=THT]
  R8 = Resistor [tolerance=±5% resistance=220 package=THT]
  R9 = Resistor [tolerance=±5% resistance=220 package=THT]
  R10 = Resistor [tolerance=±5% resistance=220 package=THT]
  R11 = Resistor [tolerance=±5% resistance=220 package="0603 [SMD]"]  # not connected
  Q5 = Basic FET N-Channel [package="D2Pak [SMD]"]
  R12 = Resistor [tolerance=±5% resistance=220 package="0603 [SMD]"]  # not connected
  R13 = Resistor [tolerance=±5% resistance=220 package="0603 [SMD]"]  # not connected
  R14 = Resistor [tolerance=±5% resistance=220 package="0603 [SMD]"]  # not connected
  VCC1 = Battery block 9V  # not connected

nets:
  GND: Composant1.ADDR, Composant1.GND, Raspberry_Pi_1.GND, R1.Pin_1, R2.Pin_1, R3.Pin_1, R4.Pin_1, D1.anode, D2.anode, Q2.source, Q3.source, Q4.source, Q5.source
  N1: Composant1.SDA, Raspberry_Pi_1.GPIO2
  N2: Composant1.SCL, Raspberry_Pi_1.GPIO3
  VDD: Composant1.VDD, Raspberry_Pi_1.3V3
  N3: Raspberry_Pi_1.GPIO6, R7.Pin_0
  N4: Raspberry_Pi_1.GPIO13, R8.Pin_0
  N5: Raspberry_Pi_1.GPIO19, R9.Pin_0
  N6: Raspberry_Pi_1.GPIO26, R10.Pin_0
  N7: Raspberry_Pi_1.GPIO24, D2.cathode, R6.Pin_0
  N8: Raspberry_Pi_1.GPIO23, D1.cathode, R5.Pin_0
  N9: Q2.Gate, R8.Pin_1
  N10: Q3.Gate, R9.Pin_1
  N11: Q4.Gate, R10.Pin_1
  N12: R7.Pin_1, Q5.Gate

custom parts:
  Adafruit ADS1115 16Bit I2C ADC: For microcontrollers without an analog-to-digital converter or when you want a higher-precision ADC, the ADS1115 provides 16-bit precision at 860 samples/second over I2C. The chip can be configured as 4 single-ended input channels, or two differential channels. As a nice bonus, it even includes a programmable gain amplifier, up to x16, to help boost up smaller single/differential signals to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
  Raspberry Pi 4: The RPi4, a faster version of the awesome Raspberry Pi 2 B ARM Board with 40 pin gpio. Ready for special Raspberry Pi B+ and RPi2 Hat (Hardware attached (on) top)
